// Logisim project New_Computer_project.circ as structural Verilog: 6 circuits, main circuit ALU
module ALU (
  input  [2:0] switch,
  input  carry_borrow_in,
  input  [31:0] data_a,
  input  [31:0] data_b,
  input  [3:0] compare_switch,
  output carry_borrow_out,
  output [31:0] data_out
);

  wire adder_1_cout, and_1_out, and_2_out, comparator_1_eq, comparator_1_gt, comparator_1_lt,
       comparator_2_eq, comparator_2_gt, comparator_2_lt, or_2_out, or_4_out, subtractor_1_bout;
  wire [15:0] bit_extender_1_out, bit_extender_3_out;
  wire [31:0] adder_1_out, and_3_out, and_4_out, and_5_out, and_6_out, and_7_out, bit_extender_2_out,
       bit_extender_4_out, bit_extender_5_out, bit_extender_6_out, multiplexer_2_out, or_3_out, or_5_out,
       or_6_out, or_7_out, or_8_out, shifter_1_out, shifter_2_out, subtractor_1_out, xor_1_out;

  or or_1 (carry_borrow_out, and_1_out, and_2_out);
  and and_1 (and_1_out, ~switch[2], ~switch[1], ~switch[0], or_2_out);  // AND_Gate
  and and_2 (and_2_out, ~switch[1], ~switch[2], switch[0], or_4_out);  // AND_Gate
  or or_2 (or_2_out, subtractor_1_bout, adder_1_cout);
  Adder #(.width(32)) adder_1 (.a(data_a), .b(data_b), .out(adder_1_out), .cin(carry_borrow_in), .cout(adder_1_cout));
  Subtractor #(.width(32)) subtractor_1 (
    .a(data_a), .b(data_b), .out(subtractor_1_out), .bin(carry_borrow_in), .bout(subtractor_1_bout));
  Comparator #(.width(32)) comparator_1 (
    .a(data_a), .b(data_b), .gt(comparator_1_gt), .eq(comparator_1_eq), .lt(comparator_1_lt));
  Shifter #(.width(32)) shifter_1 (.in(data_a), .\dist (data_b[4:0]), .out(shifter_1_out));
  Shifter #(.shift("lr"), .width(32)) shifter_2 (.in(data_a), .\dist (data_b[4:0]), .out(shifter_2_out));
  assign and_3_out = data_a & data_b;  // AND_Gate and_3, 32 bits wide
  assign or_3_out = data_a | data_b;  // OR_Gate or_3, 32 bits wide
  assign xor_1_out = data_a ^ data_b;  // XOR_Gate xor_1, 32 bits wide
  or or_4 (or_4_out, subtractor_1_bout, adder_1_cout);
  assign bit_extender_1_out = {{15{comparator_1_gt}}, comparator_1_gt};  // Bit_Extender bit_extender_1
  assign bit_extender_2_out = {{31{comparator_1_eq}}, comparator_1_eq};  // Bit_Extender bit_extender_2
  assign bit_extender_3_out = {{15{comparator_1_lt}}, comparator_1_lt};  // Bit_Extender bit_extender_3
  Multiplexer #(.select(3), .width(32)) multiplexer_1 (
    .in0(adder_1_out), .in1(subtractor_1_out), .in2(multiplexer_2_out), .in3(shifter_1_out),
    .in4(shifter_2_out), .in5(and_3_out), .in6(or_3_out), .in7(xor_1_out), .out(data_out), .sel(switch));
  assign bit_extender_4_out = {{16{comparator_1_gt}}, bit_extender_1_out};  // Bit_Extender bit_extender_4
  assign bit_extender_5_out = {{16{comparator_1_lt}}, bit_extender_3_out};  // Bit_Extender bit_extender_5
  // NoConnect on comparator_2_gt
  Comparator #(.width(32)) comparator_2 (
    .a(data_a), .b({32{1'b0}}), .gt(comparator_2_gt), .eq(comparator_2_eq), .lt(comparator_2_lt));
  // NoConnect on comparator_2_lt
  Multiplexer #(.select(4), .width(32)) multiplexer_2 (
    .in0(bit_extender_4_out), .in1(bit_extender_5_out), .in2(bit_extender_2_out), .in3(bit_extender_6_out),
    .in4({32{1'b1}}), .in5({32{1'b0}}), .in6({32{1'b0}}), .in7({32{1'b0}}), .in8(and_4_out), .in9(and_5_out),
    .in10(and_6_out), .in11(and_7_out), .in12({32{1'b0}}), .in13({32{1'b0}}), .in14({32{1'b0}}),
    .in15({32{1'b0}}), .out(multiplexer_2_out), .sel(compare_switch));
  assign and_4_out = ~bit_extender_5_out & or_5_out;  // AND_Gate and_4, 32 bits wide
  assign bit_extender_6_out = {{31{comparator_2_eq}}, comparator_2_eq};  // Bit_Extender bit_extender_6
  assign and_5_out = ~bit_extender_4_out & or_6_out;  // AND_Gate and_5, 32 bits wide
  assign or_5_out = bit_extender_4_out | bit_extender_2_out | bit_extender_6_out;  // OR_Gate or_5, 32 bits wide
  assign or_6_out = bit_extender_2_out | bit_extender_6_out | bit_extender_5_out;  // OR_Gate or_6, 32 bits wide
  assign and_6_out = ~bit_extender_2_out & or_7_out;  // AND_Gate and_6, 32 bits wide
  assign or_7_out = bit_extender_4_out | bit_extender_6_out | bit_extender_5_out;  // OR_Gate or_7, 32 bits wide
  assign and_7_out = ~bit_extender_6_out & or_8_out;  // AND_Gate and_7, 32 bits wide
  assign or_8_out = bit_extender_5_out | bit_extender_2_out | bit_extender_4_out;  // OR_Gate or_8, 32 bits wide

  // Notes on the sheet:
  //   adder
  //   subtractor
  //   comparator
  //   logical and
  //   logical or
  //   logical xor
  //   shifters
endmodule

module test (
  input  [31:0] in_1,
  input  clock,
  input  Write_Enable,
  output out_4,
  output [31:0] out_5,
  output [31:0] out_6,
  output [31:0] out_7
);

  wire dualram_1_p2, multiplexer_6_out;
  wire [2:0] multiplexer_2_out;
  wire [3:0] multiplexer_8_out;
  wire [4:0] multiplexer_4_out;
  wire [20:0] undriven;
  wire [26:0] demultiplexer_1_out0, demultiplexer_1_out1;
  wire [31:0] bit_extender_1_out, multiplexer_1_out, multiplexer_3_out, multiplexer_5_out;

  Demultiplexer #(.select(5), .width(27)) demultiplexer_1 (
    .out0(demultiplexer_1_out0), .out1(demultiplexer_1_out1), .in(in_1[31:5]), .sel(in_1[4:0]));  // open: out2, out3, out4, out5, out6, out7, out8, out9, out10, out11, out12, out13, out14, out15, out16, out17, out18, out19, out20, out21, out22, out23, out24, out25, out26, out27, out28, out29, out30, out31
  Multiplexer #(.select(5), .width(32)) multiplexer_1 (
    .in1(out_6), .out(multiplexer_1_out), .sel(in_1[4:0]));  // open: in0, in2, in3, in4, in5, in6, in7, in8, in9, in10, in11, in12, in13, in14, in15, in16, in17, in18, in19, in20, in21, in22, in23, in24, in25, in26, in27, in28, in29, in30, in31
  assign bit_extender_1_out = {{11{1'b0}}, demultiplexer_1_out0[25:5]};  // Bit_Extender bit_extender_1
  Multiplexer #(.select(5), .width(3)) multiplexer_2 (
    .in1(demultiplexer_1_out1[7:5]), .out(multiplexer_2_out), .sel(in_1[4:0]));  // open: in0, in2, in3, in4, in5, in6, in7, in8, in9, in10, in11, in12, in13, in14, in15, in16, in17, in18, in19, in20, in21, in22, in23, in24, in25, in26, in27, in28, in29, in30, in31
  Multiplexer #(.select(5), .width(32)) multiplexer_3 (
    .in0(bit_extender_1_out), .in1(out_5), .out(multiplexer_3_out), .sel(in_1[4:0]));  // open: in2, in3, in4, in5, in6, in7, in8, in9, in10, in11, in12, in13, in14, in15, in16, in17, in18, in19, in20, in21, in22, in23, in24, in25, in26, in27, in28, in29, in30, in31
  Multiplexer #(.select(5), .width(5)) multiplexer_4 (
    .in0(demultiplexer_1_out0[4:0]), .in1(demultiplexer_1_out1[4:0]), .out(multiplexer_4_out), .sel(in_1[4:0]));  // open: in2, in3, in4, in5, in6, in7, in8, in9, in10, in11, in12, in13, in14, in15, in16, in17, in18, in19, in20, in21, in22, in23, in24, in25, in26, in27, in28, in29, in30, in31
  // DualRAM #(.addrWidth(5), .dataWidth(32)) dualram_1: pin names not known; wires that end beside it: multiplexer_4_out, dualram_1_p2, clock, clock, Write_Enable, Write_Enable, multiplexer_3_out, out_6
  ALU alu_1 (
    .switch(multiplexer_2_out), .carry_borrow_in(multiplexer_6_out), .data_a(multiplexer_1_out),
    .data_b(multiplexer_5_out), .compare_switch(multiplexer_8_out), .carry_borrow_out(out_4), .data_out(out_5));
  Multiplexer #(.select(5), .width(32)) multiplexer_5 (
    .in1({demultiplexer_1_out1[18:8], undriven}), .out(multiplexer_5_out), .sel(in_1[4:0]));  // open: in0, in2, in3, in4, in5, in6, in7, in8, in9, in10, in11, in12, in13, in14, in15, in16, in17, in18, in19, in20, in21, in22, in23, in24, in25, in26, in27, in28, in29, in30, in31
  Multiplexer #(.select(5)) multiplexer_6 (
    .in1(demultiplexer_1_out1[19]), .out(multiplexer_6_out), .sel(in_1[4:0]));  // open: in0, in2, in3, in4, in5, in6, in7, in8, in9, in10, in11, in12, in13, in14, in15, in16, in17, in18, in19, in20, in21, in22, in23, in24, in25, in26, in27, in28, in29, in30, in31
  Multiplexer #(.select(5)) multiplexer_7 (
    .in0(demultiplexer_1_out0[26]), .in1(demultiplexer_1_out1[20]), .out(dualram_1_p2), .sel(in_1[4:0]));  // open: in2, in3, in4, in5, in6, in7, in8, in9, in10, in11, in12, in13, in14, in15, in16, in17, in18, in19, in20, in21, in22, in23, in24, in25, in26, in27, in28, in29, in30, in31
  Multiplexer #(.select(5), .width(4)) multiplexer_8 (
    .out(multiplexer_8_out), .sel(in_1[4:0]));  // open: in0, in1, in2, in3, in4, in5, in6, in7, in8, in9, in10, in11, in12, in13, in14, in15, in16, in17, in18, in19, in20, in21, in22, in23, in24, in25, in26, in27, in28, in29, in30, in31

  // Notes on the sheet:
  //   inst
  //   Register 5
  //   Numerical 21
  //   Register 5
  //   switch 3
  //   num 11
  //   borrow/carry
  //   write en
  //   Bottom 5
  //   Top 27
endmodule

module test2 (
  input  [31:0] instruction_address,
  input  instruction_switch,
  input  [31:0] instruction_data_in,
  input  clock,
  input  clear_pc,
  output [31:0] out_6,
  output [31:0] data_out
);

  wire alu_1_carry_borrow_out, decoder_1_out0, decoder_1_out1, demultiplexer_1_out0, demultiplexer_1_out1,
       demultiplexer_1_out2, demultiplexer_1_out3, multiplexer_4_p5, multiplexer_6_p6, multiplexer_7_p6,
       multiplexer_8_p7, multiplexer_10_p6, multiplexer_15_out, multiplexer_16_out, or_1_out, or_2_out;
  wire [2:0] demultiplexer_2_out1_2, multiplexer_5_p6;
  wire [3:0] bit_extender_1_out, multiplexer_13_out;
  wire [4:0] multiplexer_12_out;
  wire [12:0] demultiplexer_2_out1_3;
  wire [15:0] multiplexer_4_p3, multiplexer_4_p3_2, multiplexer_9_p5, multiplexer_9_p5_2;
  wire [26:0] demultiplexer_2_out0, demultiplexer_2_out1, demultiplexer_2_out2, demultiplexer_2_out3,
       demultiplexer_2_out4;
  wire [31:0] and_1_out, and_2_out, b21_32_extender_1_out_2, bit_extender_2_out, bit_extender_3_out,
       if_equal_box_1_out_2, multiplexer_2_out, multiplexer_3_out, multiplexer_9_p3, multiplexer_9_p6,
       multiplexer_11_p6, multiplexer_14_out, pc_1_data_out, ram_1_dout, ram_2_dout;

  Multiplexer #(.width(32)) multiplexer_1 (
    .in0(instruction_address), .in1(pc_1_data_out), .out(out_6), .sel(instruction_switch));
  Decoder decoder_1 (.out0(decoder_1_out0), .out1(decoder_1_out1), .sel(out_6[31]), .en(1'b1));
  RAM #(.addrWidth(16), .dataWidth(32)) ram_1 (
    .addr(out_6[15:0]), .we(decoder_1_out0), .oe(decoder_1_out0), .clk(clock), .din(instruction_data_in),
    .dout(ram_1_dout));
  RAM #(.addrWidth(15), .dataWidth(32)) ram_2 (
    .addr(out_6[30:16]), .we(decoder_1_out1), .oe(decoder_1_out1), .clk(clock), .din(instruction_data_in),
    .dout(ram_2_dout));
  Multiplexer #(.width(32)) multiplexer_2 (
    .in0(ram_1_dout), .in1(ram_2_dout), .out(multiplexer_2_out), .sel(out_6[31]));
  Demultiplexer #(.select(5)) demultiplexer_1 (
    .out0(demultiplexer_1_out0), .out1(demultiplexer_1_out1), .out2(demultiplexer_1_out2),
    .out3(demultiplexer_1_out3), .in(clock), .sel(multiplexer_2_out[31:27]));  // open: out4, out5, out6, out7, out8, out9, out10, out11, out12, out13, out14, out15, out16, out17, out18, out19, out20, out21, out22, out23, out24, out25, out26, out27, out28, out29, out30, out31
  or or_1 (or_1_out, demultiplexer_1_out0, demultiplexer_1_out1, demultiplexer_1_out2);
  or or_2 (or_2_out, or_1_out, demultiplexer_1_out3);
  Hex_Digit_Display hex_digit_display_1 (.value(multiplexer_2_out[3:0]));  // open: dp
  Hex_Digit_Display hex_digit_display_2 (.value(multiplexer_2_out[7:4]));  // open: dp
  Hex_Digit_Display hex_digit_display_3 (.value(multiplexer_2_out[11:8]));  // open: dp
  Hex_Digit_Display hex_digit_display_4 (.value(multiplexer_2_out[15:12]));  // open: dp
  Hex_Digit_Display hex_digit_display_5 (.value(multiplexer_2_out[19:16]));  // open: dp
  Hex_Digit_Display hex_digit_display_6 (.value(multiplexer_2_out[23:20]));  // open: dp
  Demultiplexer #(.select(5), .width(27)) demultiplexer_2 (
    .out0(demultiplexer_2_out0),
    .out1({demultiplexer_2_out1[26:21], demultiplexer_2_out1_3, demultiplexer_2_out1_2, demultiplexer_2_out1[4:0]}),
    .out2(demultiplexer_2_out2), .out3(demultiplexer_2_out3), .out4(demultiplexer_2_out4),
    .in(multiplexer_2_out[26:0]), .sel(multiplexer_2_out[31:27]));  // open: out5, out6, out7, out8, out9, out10, out11, out12, out13, out14, out15, out16, out17, out18, out19, out20, out21, out22, out23, out24, out25, out26, out27, out28, out29, out30, out31
  Hex_Digit_Display hex_digit_display_7 (.value(bit_extender_1_out));  // open: dp
  assign bit_extender_1_out = {{1{multiplexer_2_out[26]}}, multiplexer_2_out[26:24]};  // Bit_Extender bit_extender_1
  assign bit_extender_2_out = {{31{demultiplexer_2_out2[11]}}, demultiplexer_2_out2[11]};  // Bit_Extender bit_extender_2
  Multiplexer #(.select(5), .width(32)) multiplexer_3 (
    .in0({32{1'b0}}), .in1({32{1'b0}}), .in2(and_2_out), .in3({multiplexer_4_p3_2, multiplexer_4_p3}),
    .out(multiplexer_3_out));  // open: in4, in5, in6, in7, in8, in9, in10, in11, in12, in13, in14, in15, in16, in17, in18, in19, in20, in21, in22, in23, in24, in25, in26, in27, in28, in29, in30, in31, sel
  b21_32_extender b21_32_extender_1 (.in_1(demultiplexer_2_out0[25:5]), .out_2(b21_32_extender_1_out_2));
  // Multiplexer #(.select(5), .width(32)) multiplexer_4: pin names not known; wires that end beside it: multiplexer_2_out[31:27], b21_32_extender_1_out_2, {multiplexer_4_p3_2, multiplexer_4_p3}, {32{1'b0}}, multiplexer_4_p5, multiplexer_2_out[31:27]
  // Multiplexer #(.select(5), .width(3)) multiplexer_5: pin names not known; wires that end beside it: multiplexer_2_out[31:27], 3'b000, demultiplexer_2_out1_2, 3'b000, demultiplexer_2_out3[12:10], multiplexer_5_p6, multiplexer_2_out[31:27]
  // Multiplexer #(.select(5)) multiplexer_6: pin names not known; wires that end beside it: multiplexer_2_out[31:27], 1'b0, 1'b0, demultiplexer_2_out2[10], demultiplexer_2_out3[14], multiplexer_6_p6, multiplexer_2_out[31:27]
  // Multiplexer #(.select(5)) multiplexer_7: pin names not known; wires that end beside it: multiplexer_2_out[31:27], 1'b0, demultiplexer_2_out1[21], 1'b0, demultiplexer_2_out3[13], multiplexer_7_p6, multiplexer_2_out[31:27]
  // Multiplexer #(.select(5), .width(5)) multiplexer_8: pin names not known; wires that end beside it: multiplexer_2_out[31:27], {5{1'b0}}, {5{1'b0}}, demultiplexer_2_out2[9:5], demultiplexer_2_out3[9:5], demultiplexer_2_out4[9:5], multiplexer_8_p7, multiplexer_2_out[31:27]
  // Multiplexer #(.select(5), .width(32)) multiplexer_9: pin names not known; wires that end beside it: multiplexer_2_out[31:27], {32{1'b0}}, multiplexer_9_p3, {32{1'b0}}, {multiplexer_9_p5_2, multiplexer_9_p5}, multiplexer_9_p6, multiplexer_2_out[31:27]
  assign bit_extender_3_out = {{19{1'b0}}, demultiplexer_2_out1_3};  // Bit_Extender bit_extender_3
  If_equal_box if_equal_box_1 (.in_1(multiplexer_9_p3), .out_2(if_equal_box_1_out_2));
  // Multiplexer #(.select(5)) multiplexer_10: pin names not known; wires that end beside it: multiplexer_2_out[31:27], demultiplexer_2_out0[26], demultiplexer_2_out1[22], 1'b0, 1'b0, multiplexer_10_p6, multiplexer_2_out[31:27]
  // Multiplexer #(.select(5), .width(32)) multiplexer_11: pin names not known; wires that end beside it: multiplexer_2_out[31:27], {32{1'b0}}, bit_extender_3_out, {32{1'b0}}, multiplexer_9_p3, multiplexer_11_p6, multiplexer_2_out[31:27]
  assign and_1_out = {multiplexer_9_p5_2, multiplexer_9_p5} & if_equal_box_1_out_2;  // AND_Gate and_1, 32 bits wide
  Multiplexer #(.select(5), .width(5)) multiplexer_12 (
    .in0(demultiplexer_2_out0[4:0]), .in1(demultiplexer_2_out1[4:0]), .in2(demultiplexer_2_out2[4:0]),
    .in3(demultiplexer_2_out3[4:0]), .in4(demultiplexer_2_out4[4:0]), .out(multiplexer_12_out));  // open: in5, in6, in7, in8, in9, in10, in11, in12, in13, in14, in15, in16, in17, in18, in19, in20, in21, in22, in23, in24, in25, in26, in27, in28, in29, in30, in31, sel
  // DualRAM #(.addrWidth(5), .dataWidth(32)) dualram_1: pin names not known; wires that end beside it: multiplexer_12_out, multiplexer_10_p6, 1'b1, or_2_out, multiplexer_4_p5, multiplexer_8_p7, multiplexer_6_p6, 1'b1, or_2_out, multiplexer_3_out, multiplexer_9_p3, {multiplexer_9_p5_2, multiplexer_9_p5}
  Multiplexer #(.select(5), .width(4)) multiplexer_13 (
    .in0(4'b0000), .in1(demultiplexer_2_out1[26:23]), .in2(4'b0000), .in3(demultiplexer_2_out3[18:15]),
    .out(multiplexer_13_out));  // open: in4, in5, in6, in7, in8, in9, in10, in11, in12, in13, in14, in15, in16, in17, in18, in19, in20, in21, in22, in23, in24, in25, in26, in27, in28, in29, in30, in31, sel
  Multiplexer #(.select(5), .width(32)) multiplexer_14 (
    .in0({32{1'b0}}), .in1({32{1'b0}}), .in2({32{1'b0}}), .in3({32{1'b0}}), .in4(and_1_out),
    .out(multiplexer_14_out), .sel(multiplexer_2_out[31:27]));  // open: in5, in6, in7, in8, in9, in10, in11, in12, in13, in14, in15, in16, in17, in18, in19, in20, in21, in22, in23, in24, in25, in26, in27, in28, in29, in30, in31
  pc pc_1 (
    .clock(multiplexer_16_out), .switch(multiplexer_15_out), .data_in(multiplexer_14_out), .clear(clear_pc),
    .data_out(pc_1_data_out));
  LED led_1 (.in(alu_1_carry_borrow_out));
  ALU alu_1 (
    .switch(multiplexer_5_p6), .carry_borrow_in(multiplexer_7_p6), .data_a(multiplexer_9_p6),
    .data_b(multiplexer_11_p6), .compare_switch(multiplexer_13_out),
    .carry_borrow_out(alu_1_carry_borrow_out), .data_out({multiplexer_4_p3_2, multiplexer_4_p3}));
  Multiplexer #(.select(5)) multiplexer_15 (
    .in0(1'b0), .in1(1'b0), .in2(1'b0), .in3(1'b0), .in4(1'b1), .out(multiplexer_15_out));  // open: in5, in6, in7, in8, in9, in10, in11, in12, in13, in14, in15, in16, in17, in18, in19, in20, in21, in22, in23, in24, in25, in26, in27, in28, in29, in30, in31, sel
  assign and_2_out = multiplexer_9_p3 & ~bit_extender_2_out;  // AND_Gate and_2, 32 bits wide
  assign data_out = multiplexer_9_p3 & bit_extender_2_out;  // AND_Gate and_3, 32 bits wide
  Hex_Digit_Display hex_digit_display_8 (.value(multiplexer_4_p3[3:0]));  // open: dp
  Hex_Digit_Display hex_digit_display_9 (.value(multiplexer_4_p3_2[3:0]));  // open: dp
  Hex_Digit_Display hex_digit_display_10 (.value(multiplexer_9_p5[3:0]));  // open: dp
  Hex_Digit_Display hex_digit_display_11 (.value(multiplexer_9_p5[7:4]));  // open: dp
  Hex_Digit_Display hex_digit_display_12 (.value(multiplexer_9_p5_2[3:0]));  // open: dp
  Hex_Digit_Display hex_digit_display_13 (.value(multiplexer_9_p5_2[7:4]));  // open: dp
  Hex_Digit_Display hex_digit_display_14 (.value(multiplexer_4_p3[7:4]));  // open: dp
  Hex_Digit_Display hex_digit_display_15 (.value(multiplexer_4_p3[11:8]));  // open: dp
  Hex_Digit_Display hex_digit_display_16 (.value(multiplexer_4_p3_2[7:4]));  // open: dp
  Hex_Digit_Display hex_digit_display_17 (.value(multiplexer_4_p3_2[11:8]));  // open: dp
  Hex_Digit_Display hex_digit_display_18 (.value(multiplexer_9_p5[11:8]));  // open: dp
  Hex_Digit_Display hex_digit_display_19 (.value(multiplexer_9_p5[15:12]));  // open: dp
  Hex_Digit_Display hex_digit_display_20 (.value(multiplexer_9_p5_2[11:8]));  // open: dp
  Hex_Digit_Display hex_digit_display_21 (.value(multiplexer_9_p5_2[15:12]));  // open: dp
  Hex_Digit_Display hex_digit_display_22 (.value(multiplexer_4_p3[15:12]));  // open: dp
  Hex_Digit_Display hex_digit_display_23 (.value(multiplexer_4_p3_2[15:12]));  // open: dp
  Multiplexer #(.select(5)) multiplexer_16 (
    .in0(or_2_out), .in1(or_2_out), .in2(or_2_out), .in3(or_2_out), .out(multiplexer_16_out));  // open: in4, in5, in6, in7, in8, in9, in10, in11, in12, in13, in14, in15, in16, in17, in18, in19, in20, in21, in22, in23, in24, in25, in26, in27, in28, in29, in30, in31, sel

  // Notes on the sheet:
  //   top 1 switch
  //   mid 15 addr 2
  //   bottom 16 addr1
  //   location register 5b
  //   register 5b
  //   number 21
  //   register write en
  //   register 5b
  //   switch 3b
  //   numbers 14b
  //   carry/borrow
  //   write enable
  //   comp switch 3b
  //   register 1 5b
  //   register 2 5b
  //   write enable
  //   register/out switch
  //   register 1 5b
  //   register 2 5b
  //   switch 3b
  //   carry/borrow
  //   write enable
  //   comp_switch 4b
  //   answer reg 5b
  //   Control unit
  //   Top 5 (instructions)
  //   Bottom 27 (instruction data)
  //   access 1 data in
  //   switch
  //   write en 2
  //   carry/borrow in
  //   access 2 addr
  //   data a
  //   write en 1
  //   data b
  //   access 1 addr
  //   comp switch
  //   Program counter
endmodule

module b21_32_extender (
  input  [20:0] in_1,
  output [31:0] out_2
);

  assign out_2 = {{11{1'b0}}, in_1};  // Bit_Extender bit_extender_1
endmodule

module pc (
  input  clock,
  input  switch,
  input  [31:0] data_in,
  input  clear,
  output [31:0] data_out
);

  wire [31:0] adder_1_out, and_1_out, and_2_out, bit_extender_1_out, bit_extender_2_out, or_1_out;

  assign bit_extender_1_out = {{31{1'b0}}, 1'b1};  // Bit_Extender bit_extender_1
  assign bit_extender_2_out = {{31{switch}}, switch};  // Bit_Extender bit_extender_2
  Adder #(.width(32)) adder_1 (.a(bit_extender_1_out), .b(data_out), .out(adder_1_out), .cin(1'b0));  // open: cout
  assign and_1_out = adder_1_out & ~bit_extender_2_out;  // AND_Gate and_1, 32 bits wide
  assign and_2_out = data_in & bit_extender_2_out;  // AND_Gate and_2, 32 bits wide
  assign or_1_out = and_1_out | and_2_out;  // OR_Gate or_1, 32 bits wide
  Register #(.width(32)) register_1 (.D(or_1_out), .en(clock), .clk(clock), .Q(data_out), .clr(clear));
endmodule

// if
module If_equal_box (
  input  [31:0] in_1,
  output [31:0] out_2
);

  wire comparator_1_eq;

  Comparator #(.width(32)) comparator_1 (.a(in_1), .b({32{1'b1}}), .eq(comparator_1_eq));  // open: gt, lt
  assign out_2 = {{31{comparator_1_eq}}, comparator_1_eq};  // Bit_Extender bit_extender_1
endmodule
