// Logisim project com_prjct_2.circ as structural Verilog: 4 circuits, main circuit alu_float
module alu_float (
  input  [2:0] decocer,
  input  [31:0] data_1,
  input  [31:0] data_2,
  input  [3:0] comp_decoder,
  output [31:0] data_out
);

  wire [31:0] demultiplexer_1_out0, demultiplexer_1_out1, demultiplexer_1_out2, demultiplexer_1_out3,
       demultiplexer_1_out4, demultiplexer_1_out5, demultiplexer_1_out6, demultiplexer_1_out7,
       demultiplexer_2_out0, demultiplexer_2_out1, demultiplexer_2_out2, demultiplexer_2_out3,
       demultiplexer_2_out4, demultiplexer_2_out5, demultiplexer_2_out6, demultiplexer_2_out7,
       demultiplexer_3_out0, demultiplexer_3_out1, fpadder_1_out, fpround_1_p2, fpsubtractor_1_out,
       fptoint_1_p2, inttofp_1_p2, multiplexer_1_out, multiplexer_2_out, not_1_out, or_1_out, undriven;

  Multiplexer #(.select(3), .width(32)) multiplexer_1 (
    .in0(demultiplexer_1_out2), .in1(demultiplexer_1_out2), .in2(demultiplexer_1_out2),
    .in3(demultiplexer_1_out2), .out(multiplexer_1_out), .sel(comp_decoder[2:0]));  // open: in4, in5, in6, in7
  Multiplexer #(.select(3), .width(32)) multiplexer_2 (
    .in0(demultiplexer_2_out2), .in1(demultiplexer_2_out2), .in2(demultiplexer_2_out2), .in3({32{1'b0}}),
    .in4(demultiplexer_1_out2), .out(multiplexer_2_out), .sel(comp_decoder[2:0]));  // open: in5, in6, in7
  Demultiplexer #(.select(3), .width(32)) demultiplexer_1 (
    .out0(demultiplexer_1_out0), .out1(demultiplexer_1_out1), .out2(demultiplexer_1_out2),
    .out3(demultiplexer_1_out3), .out4(demultiplexer_1_out4), .out5(demultiplexer_1_out5),
    .out6(demultiplexer_1_out6), .out7(demultiplexer_1_out7), .in(data_1), .sel(decocer));
  Demultiplexer #(.select(3), .width(32)) demultiplexer_2 (
    .out0(demultiplexer_2_out0), .out1(demultiplexer_2_out1), .out2(demultiplexer_2_out2),
    .out3(demultiplexer_2_out3), .out4(demultiplexer_2_out4), .out5(demultiplexer_2_out5),
    .out6(demultiplexer_2_out6), .out7(demultiplexer_2_out7), .in(data_2), .sel(decocer));
  FPAdder fpadder_1 (.a(demultiplexer_1_out0), .b(demultiplexer_2_out0), .out(fpadder_1_out));
  FPSubtractor fpsubtractor_1 (.a(demultiplexer_1_out1), .b(demultiplexer_2_out1), .out(fpsubtractor_1_out));
  // FPComparator fpcomparator_1: pin names not known; wires that end beside it: demultiplexer_2_out7, demultiplexer_2_out6, demultiplexer_2_out5, demultiplexer_2_out4, demultiplexer_2_out3, multiplexer_1_out, multiplexer_2_out
  // FPToInt #(.width(32)) fptoint_1: pin names not known; wires that end beside it: demultiplexer_1_out3, fptoint_1_p2
  // IntToFP #(.mode("unsigned"), .width(32)) inttofp_1: pin names not known; wires that end beside it: demultiplexer_1_out4, inttofp_1_p2
  // FPRound fpround_1: pin names not known; wires that end beside it: demultiplexer_1_out5, fpround_1_p2
  Demultiplexer #(.width(32)) demultiplexer_3 (
    .out0(demultiplexer_3_out0), .out1(demultiplexer_3_out1), .in(undriven), .sel(comp_decoder[3]));
  assign not_1_out = ~demultiplexer_3_out1;  // NOT_Gate not_1, 32 bits wide
  assign or_1_out = demultiplexer_3_out0 | not_1_out;  // OR_Gate or_1, 32 bits wide
  Multiplexer #(.select(3), .width(32)) multiplexer_3 (
    .in0(fpadder_1_out), .in1(fpsubtractor_1_out), .in2(or_1_out), .in3(fptoint_1_p2), .in4(inttofp_1_p2),
    .in5(fpround_1_p2), .out(data_out), .sel(decocer));  // open: in6, in7
endmodule

module alu_int (
  input  [2:0] switch,
  input  carry_borrow_in,
  input  [31:0] data_a,
  input  [31:0] data_b,
  input  [3:0] compare_switch,
  output carry_borrow_out,
  output [31:0] data_out
);

  wire adder_1_cout, and_1_out, and_2_out, comparator_1_eq, comparator_1_gt, comparator_1_lt,
       comparator_2_eq, comparator_2_gt, comparator_2_lt, or_2_out, or_4_out, subtractor_1_bout;
  wire [15:0] bit_extender_1_out, bit_extender_3_out;
  wire [31:0] adder_1_out, and_3_out, and_4_out, and_5_out, and_6_out, and_7_out, bit_extender_2_out,
       bit_extender_4_out, bit_extender_5_out, bit_extender_6_out, multiplexer_2_out, or_3_out, or_5_out,
       or_6_out, or_7_out, or_8_out, shifter_1_out, shifter_2_out, subtractor_1_out, xor_1_out;

  or or_1 (carry_borrow_out, and_1_out, and_2_out);
  and and_1 (and_1_out, ~switch[2], ~switch[1], ~switch[0], or_2_out);  // AND_Gate
  and and_2 (and_2_out, ~switch[1], ~switch[2], switch[0], or_4_out);  // AND_Gate
  or or_2 (or_2_out, subtractor_1_bout, adder_1_cout);
  Adder #(.width(32)) adder_1 (.a(data_a), .b(data_b), .out(adder_1_out), .cin(carry_borrow_in), .cout(adder_1_cout));
  Subtractor #(.width(32)) subtractor_1 (
    .a(data_a), .b(data_b), .out(subtractor_1_out), .bin(carry_borrow_in), .bout(subtractor_1_bout));
  Comparator #(.width(32)) comparator_1 (
    .a(data_a), .b(data_b), .gt(comparator_1_gt), .eq(comparator_1_eq), .lt(comparator_1_lt));
  Shifter #(.width(32)) shifter_1 (.in(data_a), .\dist (data_b[4:0]), .out(shifter_1_out));
  Shifter #(.shift("lr"), .width(32)) shifter_2 (.in(data_a), .\dist (data_b[4:0]), .out(shifter_2_out));
  assign and_3_out = data_a & data_b;  // AND_Gate and_3, 32 bits wide
  assign or_3_out = data_a | data_b;  // OR_Gate or_3, 32 bits wide
  assign xor_1_out = data_a ^ data_b;  // XOR_Gate xor_1, 32 bits wide
  or or_4 (or_4_out, subtractor_1_bout, adder_1_cout);
  assign bit_extender_1_out = {{15{comparator_1_gt}}, comparator_1_gt};  // Bit_Extender bit_extender_1
  assign bit_extender_2_out = {{31{comparator_1_eq}}, comparator_1_eq};  // Bit_Extender bit_extender_2
  assign bit_extender_3_out = {{15{comparator_1_lt}}, comparator_1_lt};  // Bit_Extender bit_extender_3
  Multiplexer #(.select(3), .width(32)) multiplexer_1 (
    .in0(adder_1_out), .in1(subtractor_1_out), .in2(multiplexer_2_out), .in3(shifter_1_out),
    .in4(shifter_2_out), .in5(and_3_out), .in6(or_3_out), .in7(xor_1_out), .out(data_out), .sel(switch));
  assign bit_extender_4_out = {{16{comparator_1_gt}}, bit_extender_1_out};  // Bit_Extender bit_extender_4
  assign bit_extender_5_out = {{16{comparator_1_lt}}, bit_extender_3_out};  // Bit_Extender bit_extender_5
  // NoConnect on comparator_2_gt
  Comparator #(.width(32)) comparator_2 (
    .a(data_a), .b({32{1'b0}}), .gt(comparator_2_gt), .eq(comparator_2_eq), .lt(comparator_2_lt));
  // NoConnect on comparator_2_lt
  Multiplexer #(.select(4), .width(32)) multiplexer_2 (
    .in0(bit_extender_4_out), .in1(bit_extender_5_out), .in2(bit_extender_2_out), .in3(bit_extender_6_out),
    .in4({32{1'b1}}), .in5({32{1'b0}}), .in6({32{1'b0}}), .in7({32{1'b0}}), .in8(and_4_out), .in9(and_5_out),
    .in10(and_6_out), .in11(and_7_out), .in12({32{1'b0}}), .in13({32{1'b0}}), .in14({32{1'b0}}),
    .in15({32{1'b0}}), .out(multiplexer_2_out), .sel(compare_switch));
  assign and_4_out = ~bit_extender_5_out & or_5_out;  // AND_Gate and_4, 32 bits wide
  assign bit_extender_6_out = {{31{comparator_2_eq}}, comparator_2_eq};  // Bit_Extender bit_extender_6
  assign and_5_out = ~bit_extender_4_out & or_6_out;  // AND_Gate and_5, 32 bits wide
  assign or_5_out = bit_extender_4_out | bit_extender_2_out | bit_extender_6_out;  // OR_Gate or_5, 32 bits wide
  assign or_6_out = bit_extender_2_out | bit_extender_6_out | bit_extender_5_out;  // OR_Gate or_6, 32 bits wide
  assign and_6_out = ~bit_extender_2_out & or_7_out;  // AND_Gate and_6, 32 bits wide
  assign or_7_out = bit_extender_4_out | bit_extender_6_out | bit_extender_5_out;  // OR_Gate or_7, 32 bits wide
  assign and_7_out = ~bit_extender_6_out & or_8_out;  // AND_Gate and_7, 32 bits wide
  assign or_8_out = bit_extender_5_out | bit_extender_2_out | bit_extender_4_out;  // OR_Gate or_8, 32 bits wide

  // Notes on the sheet:
  //   adder
  //   subtractor
  //   comparator
  //   logical and
  //   logical or
  //   logical xor
  //   shifters
endmodule

module full_alu (
  input  alu_decode,
  input  write_enable,
  input  clock,
  input  [31:0] data_1,
  input  [31:0] data_2,
  input  [2:0] decoder,
  input  [3:0] compare_decoder,
  input  carry_borrow_int_only,
  output [31:0] out_9,
  output out_10,
  output [31:0] out_11
);

  wire demultiplexer_5_out1, register_5_q;
  wire [2:0] demultiplexer_3_out0, demultiplexer_3_out1, register_3_q;
  wire [3:0] demultiplexer_4_out0, demultiplexer_4_out1, register_4_q;
  wire [31:0] demultiplexer_1_out0, demultiplexer_1_out1, demultiplexer_2_out0, demultiplexer_2_out1,
       register_1_q, register_2_q;

  Register #(.width(32)) register_1 (.D(data_1), .en(write_enable), .clk(clock), .Q(register_1_q));  // open: clr
  Demultiplexer #(.width(32)) demultiplexer_1 (
    .out0(demultiplexer_1_out0), .out1(demultiplexer_1_out1), .in(register_1_q), .sel(alu_decode));
  Register #(.width(32)) register_2 (.D(data_2), .en(write_enable), .clk(clock), .Q(register_2_q));  // open: clr
  Demultiplexer #(.width(32)) demultiplexer_2 (
    .out0(demultiplexer_2_out0), .out1(demultiplexer_2_out1), .in(register_2_q), .sel(alu_decode));
  Register #(.width(3)) register_3 (.D(decoder), .en(write_enable), .clk(clock), .Q(register_3_q));  // open: clr
  Demultiplexer #(.width(3)) demultiplexer_3 (
    .out0(demultiplexer_3_out0), .out1(demultiplexer_3_out1), .in(register_3_q), .sel(alu_decode));
  Register #(.width(4)) register_4 (
    .D(compare_decoder), .en(write_enable), .clk(clock), .Q(register_4_q));  // open: clr
  Demultiplexer #(.width(4)) demultiplexer_4 (
    .out0(demultiplexer_4_out0), .out1(demultiplexer_4_out1), .in(register_4_q), .sel(alu_decode));
  Register #(.width(1)) register_5 (
    .D(carry_borrow_int_only), .en(write_enable), .clk(clock), .Q(register_5_q));  // open: clr
  Demultiplexer demultiplexer_5 (.out1(demultiplexer_5_out1), .in(register_5_q), .sel(alu_decode));  // open: out0
  alu_float alu_float_1 (
    .decocer(demultiplexer_3_out0), .data_1(demultiplexer_1_out0), .data_2(demultiplexer_2_out0),
    .comp_decoder(demultiplexer_4_out0), .data_out(out_9));
  alu_int alu_int_1 (
    .switch(demultiplexer_3_out1), .carry_borrow_in(demultiplexer_5_out1), .data_a(demultiplexer_1_out1),
    .data_b(demultiplexer_2_out1), .compare_switch(demultiplexer_4_out1), .carry_borrow_out(out_10),
    .data_out(out_11));
endmodule

module test (
);

  // full_alu full_alu_1: pin names not known
endmodule
